# Fritzing sketch Circuit Connection on FritzingSoftware (saved by Fritzing 0.9.3b)
breadboards: 1

parts:
  Part1 = Arduino Uno (Rev3) - ICSP
  LED1 = LED - 3mm [color="Red (633nm)" package="3 mm [THT]"]
  LED2 = LED - 3mm [color="Red (633nm)" package="3 mm [THT]"]
  R1 = Resistor [tolerance=±5% resistance=220 package="0805 [SMD]"]
  R2 = Resistor [tolerance=±5% resistance=220 package="0805 [SMD]"]
  S1 = Pushbutton [package=THT]
  J1 = Piezo Speaker
  R3 = Photocell (LDR) [package=THT]
  R4 = Resistor [tolerance=±5% resistance=220 package="0805 [SMD]"]

nets:
  N1: Part1.A0, R3.pin_1, R4.Pin_0
  N2: Part1.A2, S1.leg0
  N3: Part1.D8, LED1.anode
  N4: Part1.D9_PWM, J1.pin2
  N5: Part1.D7, LED2.anode
  N6: Part1.5V, S1.leg1, R4.Pin_1
  N7: Part1.GND, R1.Pin_0, R2.Pin_0, J1.pin1, R3.pin_0
  N8: LED1.cathode, R2.Pin_1
  N9: LED2.cathode, R1.Pin_1
